# Fritzing sketch WRO_inge (saved by Fritzing 0.9.3b)
breadboards: 1

parts:
  ArduinoUno = Arduino Uno (Rev3)
  Driver_L293D = L293D [package=THT]
  ServoMotor = Basic Servo
  Motor1 = DC Motor
  Batería = Battery block 9V
  Componente1 = Adafruit TCS34725 RGB Color Sensor [part_number="Adafruit #1334"]
  HC-SR04_Sensor_1 = HC-SR04 Ultrasonic Distance Sensor

nets:
  N1: ArduinoUno.A4/SDA, Componente1.SDA
  N2: ArduinoUno.A5/SCL, Componente1.SCL
  N3: ArduinoUno.D9_PWM, ServoMotor.pulse
  N4: ArduinoUno.D5_PWM, HC-SR04_Sensor_1.TRIG
  N5: ArduinoUno.D6_PWM, HC-SR04_Sensor_1.ECHO
  VCC: ArduinoUno.5V, ArduinoUno.VIN, ServoMotor.vcc, Componente1.+3V3, HC-SR04_Sensor_1.VCC
  GND: ArduinoUno.GND, Driver_L293D.0V, ServoMotor.gnd, Batería.-, Componente1.GND, HC-SR04_Sensor_1.GND
  N6: Driver_L293D.In_1, Motor1.pin_2
  N7: Driver_L293D.Out_1_(_Controlled_by_Enable_1_), Motor1.pin_1
  N8: Driver_L293D.+Vmotor, Batería.+

notes:
  Equipo JARCVIS
  7.4 V

custom parts:
  Adafruit TCS34725 RGB Color Sensor: Your electronics can now see in dazzling color with this lovely color light sensor. We found the best color sensor on the market, the TCS34725, which has RGB and Clear light sensing elements. An IR blocking filter, integrated on-chip and localized to the color sensing photodiodes, minimizes the IR spectral component of the incoming light and allows color measurements to be made accurately. The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
